# Fritzing sketch coin (saved by Fritzing 0.9.3b)
breadboards: 1

parts:
  Part2 = Coin Acceptor - 6-Coin version
  Raspberry_Pi_1 = Raspberry Pi 3 [part_number=RPI-3-V1.2]
  LED1 = smd LED [color="Red (633nm)" package="0805 [SMD]"]

nets:
  GND: Part2.GND, Raspberry_Pi_1.GND, LED1.cathode
  N1: Part2.SIG, Raspberry_Pi_1.GPIO11
  N2: Raspberry_Pi_1.GPIO26, LED1.anode

notes:
  coinPin
  Connect 12v PowerSupply

custom parts:
  Coin Acceptor - 6-Coin version: 12V coin acceptor that can handle up to 6 different denominations. Output is either pulse width, serial, or single pin per coin value.
